# Fritzing sketch networkit_demo_wiring_diagram (saved by Fritzing 0.9.3b)
breadboards: 1

parts:
  Part1 = Arduino Mega ADK (Rev3)
  S1 = Momentary Switch [package=ksa_sealed_tac_switch]
  LED1 = LEDs [package=led10mm]
  R1 = Resistor [tolerance=±5% resistance=220 package="0603 [SMD]"]

nets:
  N1: Part1.GND, S1.1, R1.Pin_0
  N2: Part1.D2_PWM, LED1.A
  N3: LED1.C, R1.Pin_1
